// Logisim project logisim_minirv_CPU.circ as structural Verilog: 8 circuits, main circuit pc
module main (
  input  rst,
  input  clk,
  input  in_3,
  input  in_4,
  input  in_5,
  output [23:0] out_6,
  output [31:0] pc1,
  output [31:0] pc_in1,
  output [23:0] rom_addr1,
  output [4:0] rd_1,
  output [4:0] rs1_1,
  output [4:0] rs2_1,
  output [31:0] immU1,
  output [31:0] immI1,
  output [31:0] immS1,
  output out_16,
  output [19:0] out_17,
  output [31:0] out_18,
  output [31:0] rdata1_1,
  output [31:0] rdata2_2,
  output [31:0] add_rst1,
  output [31:0] wdata
);

  wire add, addi, and_4_out, and_5_out, and_6_out, and_16_out, and_17_out, and_18_out, comparator_1_eq,
       comparator_1_gt, comparator_2_lt, decoder_1_out0, decoder_1_out1, decoder_1_out2, decoder_1_out3,
       ebreak, jalr, lbu, lui, lw, not_2_out, not_3_out, not_4_out, not_5_out, or_2_out, or_6_out, or_7_out,
       or_8_out, or_9_out, or_10_out, or_11_out, or_12_out, sb, sw, wen;
  wire [1:0] bit_extender_10_out;
  wire [4:0] bit_extender_14_out, bit_extender_17_out, shifter_2_out, shifter_5_out;
  wire [7:0] bit_extender_12_out, bit_extender_13_out, shifter_1_out;
  wire [31:0] and_1_out, and_2_out, and_3_out, and_7_out, and_8_out, and_9_out, and_10_out, and_11_out,
       and_12_out, and_13_out, and_14_out, and_15_out, and_19_out, and_20_out, bit_extender_1_out,
       bit_extender_2_out, bit_extender_3_out, bit_extender_4_out, bit_extender_5_out, bit_extender_6_out,
       bit_extender_7_out, bit_extender_8_out, bit_extender_9_out, bit_extender_11_out, bit_extender_15_out,
       bit_extender_16_out, lbu_rst, lw_rst, not_1_out, or_3_out, pc_next_dft, rom_1_data, shifter_4_out,
       shifter_6_out, vga_x_y_1_x, vga_x_y_1_y;
  wire [31:24] shifter_3_out;

  Counter #(.max('h99520), .width(20)) counter_1 (
    .clr(in_3), .up(in_4), .count(in_5), .clk(and_4_out), .carry(out_16), .Q(out_17));  // open: load, D
  assign bit_extender_1_out = {{31{jalr}}, jalr};  // Bit_Extender bit_extender_1
  assign and_1_out = add_rst1 & 32'hffffffe;  // AND_Gate and_1, 32 bits wide
  assign not_1_out = ~bit_extender_1_out;  // NOT_Gate not_1, 32 bits wide
  not not_2 (not_2_out, out_16);
  assign and_2_out = bit_extender_1_out & and_1_out;  // AND_Gate and_2, 32 bits wide
  assign and_3_out = pc_next_dft & not_1_out;  // AND_Gate and_3, 32 bits wide
  and and_4 (and_4_out, clk, not_2_out);
  assign pc_in1 = and_2_out | and_3_out;  // OR_Gate or_1, 32 bits wide
  ROM #(.addrWidth(24), .dataWidth(32)) rom_1 (.addr(rom_addr1), .data(rom_1_data));
  or or_2 (or_2_out, sw, sb);
  pc pc_1 (.rst(rst), .pc_in(pc_in1), .WE(1'b1), .clk(and_4_out), .pc_out(pc1));
  GPR gpr_1 (
    .raddr1(rs1_1), .clk(and_4_out), .wdata(wdata), .wen(wen), .waddr(rd_1), .rst(rst), .raddr2(rs2_1),
    .rdata1(rdata1_1), .rdata2(rdata2_2));
  assign bit_extender_2_out = {{31{add}}, add};  // Bit_Extender bit_extender_2
  not not_3 (not_3_out, add);
  not not_4 (not_4_out, or_2_out);
  Shifter #(.shift("lr"), .width(32)) shifter_1 (.in(pc1), .\dist (5'b00010), .out({shifter_1_out, rom_addr1}));
  and and_5 (and_5_out, not_3_out, or_2_out);
  and and_6 (and_6_out, not_4_out, not_3_out);
  Adder #(.width(32)) adder_1 (.a(pc1), .b(32'h4), .out(pc_next_dft));  // open: cin, cout
  assign and_7_out = rdata2_2 & bit_extender_2_out;  // AND_Gate and_7, 32 bits wide
  assign bit_extender_3_out = {{31{and_5_out}}, and_5_out};  // Bit_Extender bit_extender_3
  assign bit_extender_4_out = {{31{and_6_out}}, and_6_out};  // Bit_Extender bit_extender_4
  decode decode_1 (
    .instr(rom_1_data), .lw(lw), .lbu(lbu), .rd(rd_1), .addi(addi), .rs1(rs1_1), .rs2(rs2_1), .sb(sb),
    .sw(sw), .immU(immU1), .add(add), .immI(immI1), .immS(immS1), .lui(lui), .jalr(jalr), .ebreak(ebreak));
  assign and_8_out = bit_extender_3_out & immS1;  // AND_Gate and_8, 32 bits wide
  assign and_9_out = bit_extender_4_out & immI1;  // AND_Gate and_9, 32 bits wide
  assign or_3_out = and_7_out | and_8_out | and_9_out;  // OR_Gate or_3, 32 bits wide
  or or_4 (wen, lw, lbu, addi, add, lui, jalr);
  Adder #(.width(32)) adder_2 (.a(rdata1_1), .b(or_3_out), .out(add_rst1));  // open: cin, cout
  assign bit_extender_5_out = {{31{lui}}, lui};  // Bit_Extender bit_extender_5
  assign bit_extender_6_out = {{31{add}}, add};  // Bit_Extender bit_extender_6
  assign bit_extender_7_out = {{31{addi}}, addi};  // Bit_Extender bit_extender_7
  assign bit_extender_8_out = {{31{lw}}, lw};  // Bit_Extender bit_extender_8
  assign bit_extender_9_out = {{31{lbu}}, lbu};  // Bit_Extender bit_extender_9
  Bit_Extender #(.in_width(32), .out_width(2), .\type ("zero")) bit_extender_10 (
    .in(add_rst1), .out(bit_extender_10_out));
  assign bit_extender_11_out = {{31{jalr}}, jalr};  // Bit_Extender bit_extender_11
  assign and_10_out = bit_extender_5_out & immU1;  // AND_Gate and_10, 32 bits wide
  assign and_11_out = bit_extender_6_out & add_rst1;  // AND_Gate and_11, 32 bits wide
  assign and_12_out = bit_extender_7_out & add_rst1;  // AND_Gate and_12, 32 bits wide
  assign and_13_out = bit_extender_11_out & pc_next_dft;  // AND_Gate and_13, 32 bits wide
  assign and_14_out = bit_extender_8_out & lw_rst;  // AND_Gate and_14, 32 bits wide
  assign and_15_out = bit_extender_9_out & lbu_rst;  // AND_Gate and_15, 32 bits wide
  Comparator #(.width(32)) comparator_1 (
    .a(add_rst1), .b(32'h20000000), .gt(comparator_1_gt), .eq(comparator_1_eq));  // open: lt
  Comparator #(.width(32)) comparator_2 (.a(add_rst1), .b(32'h20040000), .lt(comparator_2_lt));  // open: gt, eq
  assign wdata = and_10_out | and_11_out | and_12_out | and_13_out | and_14_out | and_15_out;  // OR_Gate or_5, 32 bits wide
  VGA_X_Y vga_x_y_1 (.addr(add_rst1), .X(vga_x_y_1_x), .Y(vga_x_y_1_y));
  or or_6 (or_6_out, comparator_1_gt, comparator_1_eq);
  Bit_Extender #(.in_width(32), .out_width(8), .\type ("zero")) bit_extender_12 (
    .in(vga_x_y_1_x), .out(bit_extender_12_out));
  Bit_Extender #(.in_width(32), .out_width(8), .\type ("zero")) bit_extender_13 (
    .in(vga_x_y_1_y), .out(bit_extender_13_out));
  and and_16 (and_16_out, or_6_out, comparator_2_lt);
  not not_5 (not_5_out, and_16_out);
  and and_17 (and_17_out, sw, and_16_out);
  Decoder #(.select(2)) decoder_1 (
    .out0(decoder_1_out0), .out1(decoder_1_out1), .out2(decoder_1_out2), .out3(decoder_1_out3),
    .sel(bit_extender_10_out), .en(sb));
  // RGB_Video #(.cursor("No Cursor"), .height(256), .width(256)) rgb_video_1: pin names not known; wires that end beside it: rst, clk, and_17_out, bit_extender_12_out, bit_extender_13_out, rdata2_2[23:0]
  or or_7 (or_7_out, sb, sw);
  assign bit_extender_14_out = {{3{1'b0}}, bit_extender_10_out};  // Bit_Extender bit_extender_14
  or or_8 (or_8_out, lw, lbu);
  or or_9 (or_9_out, sw, decoder_1_out0);
  or or_10 (or_10_out, sw, decoder_1_out1);
  or or_11 (or_11_out, sw, decoder_1_out2);
  or or_12 (or_12_out, sw, decoder_1_out3);
  Shifter #(.width(5)) shifter_2 (.in(bit_extender_14_out), .\dist (3'b011), .out(shifter_2_out));
  assign bit_extender_15_out = {{31{sb}}, sb};  // Bit_Extender bit_extender_15
  assign bit_extender_16_out = {{31{sw}}, sw};  // Bit_Extender bit_extender_16
  Shifter #(.shift("lr"), .width(32)) shifter_3 (.in(add_rst1), .\dist (5'b00010), .out({shifter_3_out, out_6}));
  and and_18 (and_18_out, not_5_out, or_7_out);
  Shifter #(.width(32)) shifter_4 (.in(rdata2_2), .\dist (shifter_2_out), .out(shifter_4_out));
  RAM #(.addrWidth(24), .asyncread("true"), .byteenables("byteEnables"), .dataWidth(32), .\type ("nonvolatile")) ram_1 (
    .addr(out_6), .we(and_18_out), .oe(or_8_out), .clk(and_4_out), .din(out_18), .dout(lw_rst),
    .be3(or_12_out), .be2(or_11_out), .be1(or_10_out), .be0(or_9_out));
  assign and_19_out = shifter_4_out & bit_extender_15_out;  // AND_Gate and_19, 32 bits wide
  assign and_20_out = rdata2_2 & bit_extender_16_out;  // AND_Gate and_20, 32 bits wide
  assign out_18 = and_19_out | and_20_out;  // OR_Gate or_13, 32 bits wide
  assign bit_extender_17_out = {{3{1'b0}}, bit_extender_10_out};  // Bit_Extender bit_extender_17
  Shifter #(.width(5)) shifter_5 (.in(bit_extender_17_out), .\dist (3'b011), .out(shifter_5_out));
  Shifter #(.shift("lr"), .width(32)) shifter_6 (.in(lw_rst), .\dist (shifter_5_out), .out(shifter_6_out));
  // NoConnect on shifter_6_out[15:8]
  // NoConnect on shifter_6_out[23:16]
  // NoConnect on shifter_6_out[31:24]
  assign lbu_rst = {{24{1'b0}}, shifter_6_out[7:0]};  // Bit_Extender bit_extender_18

  // Other names for the same wires on the sheet: add_rst[31:0] = add_rst1; immI[31:0] = immI1; immS[31:0] = immS1;
  //   immU[31:0] = immU1; raddr1[4:0] = rs1_1; raddr2[4:0] = rs2_1; rdata2[31:0] = rdata2_2; waddr[4:0] = rd_1

  // Notes on the sheet:
  //   contents of rom_1 (hex, n*v repeats v):
  //   413 93137 10113 10b7 dbc08093 80e7 fe012823 fea10923 fea12423 fe914203 fe4109a3 ff012783 f787b3
  //   f787b3 4b6b7 f0068693 fdc10113 d787b3 10000713 f12423 10593 100793 b00513 2112023 12023 12223 e12623
  //   e12823 f10a23 10b7 a8408093 80e7 2012083 2410113 8067 ff410113 112423 10b7 a7c08093 80e7 513 1800093
  //   80e7 812083 513 c10113 8067 852583 feb12823 fe812e23 3437 a0840413 ff014183 3401b3 1c183 ff114203
  //   440233 24203 4181b3 ff214203 440233 24203 4181b3 ff314203 440233 24203 4181b3 3237 a0020213 320233
  //   24203 ffc12403 420233 420233 410233 11b7 85c18193 fe312823 14800193 fe312623 fec22203 20067 1052703
  //   52683 452783 fe810113 e12423 112a23 fed12823 fef12623 13737 c0070713 fe012223 ff314203 fe4102a3
  //   fef14203 fe410223 fe412203 470233 24203 fe4105a3 ff214203 fe4102a3 fee14203 fe410223 fe412203 470233
  //   24203 fe410523 ff114203 fe4102a3 fed14203 fe410223 fe412203 470233 24203 fe4104a3 ff014203 fe4102a3
  //   fec14203 fe410223 fe412203 470233 24203 fe410423 fe812703 c52603 fee12823 fe812e23 3437 a0840413
  //   ff014183 3401b3 1c183 ff114203 440233 24203 4181b3 ff214203 440233 24203 4181b3 ff314203 440233
  //   24203 4181b3 3237 a0020213 320233 24203 ffc12403 420233 420233 410233 66800193 fe312823 28000193
  //   fe312623 fec22203 20067 c68733 10000513 fe812e23 fe912c23 fee12823 50413 ff012483 fe812423 feb14183
  //   3181b3 fe312423 fe914183 3181b3 fe912423 feb14203 420233 fe412423 fe914203 4181b3 3181b3 fe312a23
  //   fe912423 33237 b0020213 feb14183 4181b3 1c183 fe3103a3 fea14183 4181b3 1c183 fe310323 fe914183
  //   4181b3 1c183 fe3102a3 fe814183 4181b3 1c183 fe310223 ff412183 fe412203 440233 120213 fe412423
  //   feb14203 420233 fe412423 fe914203 4181b3 3237 b0820213 320233 ff812483 ffc12403 24203 420233 420233
  //   410233 11b7 86018193 fe312823 38800193 fe312623 fec22203 20067 812703 10000513 812823 e78733
  //   fe812e23 fe912c23 fee12823 50413 ff012483 fe812423 feb14183 3181b3 fe312423 fe914183 3181b3 fe912423
  //   feb14203 420233 fe412423 fe914203 4181b3 3181b3 fe312a23 fe912423 33237 b0020213 feb14183 4181b3
  //   1c183 fe3103a3 fea14183 4181b3 1c183 fe310323 fe914183 4181b3 1c183 fe3102a3 fe814183 4181b3 1c183
  //   fe310223 ff412183 fe412203 440233 120213 fe412423 feb14203 420233 fe412423 fe914203 4181b3 3237
  //   b0820213 320233 ff812483 ffc12403 24203 420233 420233 410233 11b7 86418193 fe312823 49800193
  //   fe312623 fec22203 20067 8*f787b3 d787b3 f787b3 f787b3 20000437 f40433 812783 c60633 c60633 fef12423
  //   feb14183 3181b3 fe312423 fe914183 fff78213 fe412423 feb14203 420233 fe412423 fe914203 4181b3 3237
  //   b1820213 418233 24203 420233 420233 410233 65800193 fe312823 53c00193 fe312623 fec22203 20067 912623
  //   493 40513 c12223 b12023 10b7 de008093 80e7 12583 412603 812783 148493 40040413 c585b3 fef12823
  //   fe912623 fe812e23 fe912c23 4b437 d0040413 ff014183 340233 100193 320023 fec14183 3401b3 18023 24183
  //   ff114483 940233 100493 920023 fed14483 9404b3 48023 24483 9181b3 ff214483 940233 100493 920023
  //   fee14483 9404b3 48023 24483 9181b3 ff314483 940233 100493 920023 fef14483 9404b3 48023 24483 9181b3
  //   3237 a0020213 320233 24203 ff812483 ffc12403 420233 420233 410233 65400193 fe312823 54400193
  //   fe312623 fec22203 20067 c12483 1012403 1412083 1810113 8067 10000713 fec12823 fee12623 fe812e23
  //   fe912c23 4b437 d0040413 ff014183 340233 100193 320023 fec14183 3401b3 18023 24183 ff114483 940233
  //   100493 920023 fed14483 9404b3 48023 24483 9181b3 ff214483 940233 100493 920023 fee14483 9404b3 48023
  //   24483 9181b3 ff314483 940233 100493 920023 fef14483 9404b3 48023 24483 9181b3 3237 a0020213 320233
  //   24203 ff812483 ffc12403 420233 420233 410233 74c00193 fe312823 28000193 fe312623 fec22203 20067
  //   812703 fee12823 fec12623 fe812e23 fe912c23 4b437 d0040413 ff014183 340233 100193 320023 fec14183
  //   3401b3 18023 24183 ff114483 940233 100493 920023 fed14483 9404b3 48023 24483 9181b3 ff214483 940233
  //   100493 920023 fee14483 9404b3 48023 24483 9181b3 ff314483 940233 100493 920023 fef14483 9404b3 48023
  //   24483 9181b3 3237 a0020213 320233 24203 ff812483 ffc12403 420233 420233 410233 11b7 83418193
  //   fe312823 38800193 fe312623 fec22203 20067 1412083 40637 20000537 1810113 1237 de020213 20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
  //   Decode 无问题
endmodule

module pc (
  input  rst,
  input  [31:0] pc_in,
  input  WE,
  input  clk,
  output [31:0] pc_out
);

  wire not_1_out;
  wire [31:0] and_1_out, bit_extender_1_out;

  not not_1 (not_1_out, rst);
  assign bit_extender_1_out = {{31{not_1_out}}, not_1_out};  // Bit_Extender bit_extender_1
  assign and_1_out = bit_extender_1_out & pc_in;  // AND_Gate and_1, 32 bits wide
  Register #(.width(32)) pc (.D(and_1_out), .en(WE), .clk(clk), .Q(pc_out));  // open: clr
endmodule

module decode (
  input  [31:0] instr,
  output lw,
  output lbu,
  output [4:0] rd,
  output addi,
  output [4:0] rs1,
  output [4:0] rs2,
  output sb,
  output sw,
  output [31:0] immU,
  output add,
  output [31:0] immI,
  output [31:0] immS,
  output lui,
  output jalr,
  output ebreak
);

  wire decoder_1_out3, decoder_1_out35, decoder_2_out2, decoder_2_out4, decoder_3_out0, decoder_3_out2;

  decode_imm decode_imm_1 (.instr(instr), .immU(immU), .immI(immI), .immS(immS));
  Decoder #(.select(7)) decoder_1 (
    .out3(decoder_1_out3), .out19(addi), .out35(decoder_1_out35), .out51(add), .out55(lui), .out103(jalr),
    .out115(ebreak), .sel(instr[6:0]), .en(1'b1));  // open: out0, out1, out2, out4, out5, out6, out7, out8, out9, out10, out11, out12, out13, out14, out15, out16, out17, out18, out20, out21, out22, out23, out24, out25, out26, out27, out28, out29, out30, out31, out32, out33, out34, out36, out37, out38, out39, out40, out41, out42, out43, out44, out45, out46, out47, out48, out49, out50, out52, out53, out54, out56, out57, out58, out59, out60, out61, out62, out63, out64, out65, out66, out67, out68, out69, out70, out71, out72, out73, out74, out75, out76, out77, out78, out79, out80, out81, out82, out83, out84, out85, out86, out87, out88, out89, out90, out91, out92, out93, out94, out95, out96, out97, out98, out99, out100, out101, out102, out104, out105, out106, out107, out108, out109, out110, out111, out112, out113, out114, out116, out117, out118, out119, out120, out121, out122, out123, out124, out125, out126, out127
  Decoder #(.select(3)) decoder_2 (
    .out2(decoder_2_out2), .out4(decoder_2_out4), .sel(instr[14:12]), .en(1'b1));  // open: out0, out1, out3, out5, out6, out7
  Decoder #(.select(3)) decoder_3 (
    .out0(decoder_3_out0), .out2(decoder_3_out2), .sel(instr[14:12]), .en(1'b1));  // open: out1, out3, out4, out5, out6, out7
  and and_1 (lw, decoder_1_out3, decoder_2_out2);
  and and_2 (lbu, decoder_2_out4, decoder_1_out3);
  and and_3 (sb, decoder_1_out35, decoder_3_out0);
  and and_4 (sw, decoder_3_out2, decoder_1_out35);

  assign rd = instr[11:7];
  assign rs1 = instr[19:15];
  assign rs2 = instr[24:20];

  // Other names for the same wires on the sheet: funct3[2:0] = instr[14:12]
endmodule

module bin_seg (
  input  D,
  input  in_2,
  input  in_3,
  input  A,
  output g,
  output f,
  output e,
  output out_8,
  output c,
  output b,
  output out_11
);

  wire and_1_out, and_2_out, and_3_out, and_4_out, and_5_out, and_6_out, and_7_out, and_8_out, and_9_out,
       and_10_out, and_11_out, and_12_out, and_13_out, and_14_out, and_15_out, and_16_out, and_17_out,
       and_18_out, and_19_out, and_20_out, and_21_out, and_22_out, and_23_out, and_24_out, and_25_out,
       and_26_out, and_27_out, and_28_out, and_29_out, and_30_out, and_31_out, and_32_out, and_33_out,
       and_34_out, and_35_out, not_1_out, not_2_out, not_3_out, not_4_out;

  not not_1 (not_1_out, D);
  not not_2 (not_2_out, in_2);
  not not_3 (not_3_out, in_3);
  not not_4 (not_4_out, A);
  and and_1 (and_1_out, not_2_out, not_4_out);
  and and_2 (and_2_out, not_1_out, in_3);
  and and_3 (and_3_out, not_1_out, in_2, A);
  and and_4 (and_4_out, D, not_2_out, not_3_out);
  and and_5 (and_5_out, D, not_4_out);
  and and_6 (and_6_out, in_2, in_3);
  and and_7 (and_7_out, not_1_out, not_3_out, not_4_out);
  and and_8 (and_8_out, not_1_out, in_3, A);
  and and_9 (and_9_out, not_2_out, not_4_out);
  and and_10 (and_10_out, D, not_3_out, A);
  and and_11 (and_11_out, not_1_out, not_2_out);
  and and_12 (and_12_out, not_1_out, in_2);
  and and_13 (and_13_out, D, not_2_out);
  and and_14 (and_14_out, not_3_out, A);
  and and_15 (and_15_out, not_2_out, not_3_out);
  and and_16 (and_16_out, not_2_out, A);
  and and_17 (and_17_out, in_2, not_3_out, A);
  and and_18 (and_18_out, not_1_out, not_2_out, not_4_out);
  and and_19 (and_19_out, not_2_out, in_3, A);
  and and_20 (and_20_out, D, not_3_out);
  and and_21 (and_21_out, in_2, in_3, not_4_out);
  and and_22 (and_22_out, not_2_out, not_4_out);
  and and_23 (and_23_out, in_3, not_4_out);
  and and_24 (and_24_out, D, in_3);
  and and_25 (and_25_out, D, in_2);
  and and_26 (and_26_out, not_3_out, not_4_out);
  and and_27 (and_27_out, not_1_out, in_2, not_3_out);
  and and_28 (and_28_out, in_2, not_4_out);
  and and_29 (and_29_out, D, not_2_out);
  and and_30 (and_30_out, D, in_3);
  and and_31 (and_31_out, not_2_out, in_3);
  and and_32 (and_32_out, D, not_2_out);
  and and_33 (and_33_out, not_1_out, in_2, not_3_out);
  and and_34 (and_34_out, in_3, not_4_out);
  and and_35 (and_35_out, D, A);
  or or_1 (g, and_1_out, and_2_out, and_3_out, and_4_out, and_5_out, and_6_out);
  or or_2 (f, and_7_out, and_8_out, and_9_out, and_10_out, and_11_out);
  or or_3 (e, and_12_out, and_13_out, and_14_out, and_15_out, and_16_out);
  or or_4 (out_8, and_17_out, and_18_out, and_19_out, and_20_out, and_21_out);
  or or_5 (c, and_22_out, and_23_out, and_24_out, and_25_out);
  or or_6 (b, and_26_out, and_27_out, and_28_out, and_29_out, and_30_out);
  or or_7 (out_11, and_31_out, and_32_out, and_33_out, and_34_out, and_35_out);
endmodule

module decode_imm (
  input  [31:0] instr,
  output [31:0] immU,
  output [31:0] immI,
  output [31:0] immS
);

  assign immI[31:11] = {{20{instr[31]}}, instr[31]};  // Bit_Extender bit_extender_1

  assign immI[10:0] = instr[30:20];
  assign immS = {immI[31:11], instr[30:25], instr[11:7]};
  assign immU = {instr[31:12], {12{1'b0}}};
endmodule

module GPR (
  input  [4:0] raddr1,
  input  clk,
  input  [31:0] wdata,
  input  wen,
  input  [4:0] waddr,
  input  rst,
  input  [4:0] raddr2,
  output [31:0] rdata1,
  output [31:0] rdata2
);

  wire and_2_out, decoder_1_out0, decoder_1_out1, decoder_1_out2, decoder_1_out3, decoder_1_out4,
       decoder_1_out5, decoder_1_out6, decoder_1_out7, decoder_1_out8, decoder_1_out9, decoder_1_out10,
       decoder_1_out11, decoder_1_out12, decoder_1_out13, decoder_1_out14, decoder_1_out15, decoder_2_out0,
       decoder_2_out1, decoder_2_out2, decoder_2_out3, decoder_2_out4, decoder_2_out5, decoder_2_out6,
       decoder_2_out7, decoder_2_out8, decoder_2_out9, decoder_2_out10, decoder_2_out11, decoder_2_out12,
       decoder_2_out13, decoder_2_out14, decoder_2_out15, not_1_out, not_2_out, not_3_out;
  wire [4:0] and_1_out, bit_extender_1_out;
  wire [31:0] and_3_out, and_4_out, and_5_out, and_6_out, bit_extender_2_out, bit_extender_3_out,
       bit_extender_4_out, bit_extender_5_out, multiplexer_1_out, multiplexer_2_out, multiplexer_3_out,
       multiplexer_4_out, register_1_q, register_2_q, register_3_q, register_4_q, register_5_q, register_6_q,
       register_7_q, register_8_q, register_9_q, register_10_q, register_11_q, register_12_q, register_13_q,
       register_14_q, register_15_q, register_16_q, register_17_q, register_18_q, register_19_q,
       register_20_q, register_21_q, register_22_q, register_23_q, register_24_q, register_25_q,
       register_26_q, register_27_q, register_28_q, register_29_q, register_30_q, register_31_q,
       register_32_q;

  assign bit_extender_1_out = {{4{wen}}, wen};  // Bit_Extender bit_extender_1
  assign and_1_out = bit_extender_1_out & waddr;  // AND_Gate and_1, 5 bits wide
  not not_1 (not_1_out, and_1_out[4]);
  Decoder #(.select(4)) decoder_1 (
    .out0(decoder_1_out0), .out1(decoder_1_out1), .out2(decoder_1_out2), .out3(decoder_1_out3),
    .out4(decoder_1_out4), .out5(decoder_1_out5), .out6(decoder_1_out6), .out7(decoder_1_out7),
    .out8(decoder_1_out8), .out9(decoder_1_out9), .out10(decoder_1_out10), .out11(decoder_1_out11),
    .out12(decoder_1_out12), .out13(decoder_1_out13), .out14(decoder_1_out14), .out15(decoder_1_out15),
    .sel(and_1_out[3:0]), .en(not_1_out));
  Decoder #(.select(4)) decoder_2 (
    .out0(decoder_2_out0), .out1(decoder_2_out1), .out2(decoder_2_out2), .out3(decoder_2_out3),
    .out4(decoder_2_out4), .out5(decoder_2_out5), .out6(decoder_2_out6), .out7(decoder_2_out7),
    .out8(decoder_2_out8), .out9(decoder_2_out9), .out10(decoder_2_out10), .out11(decoder_2_out11),
    .out12(decoder_2_out12), .out13(decoder_2_out13), .out14(decoder_2_out14), .out15(decoder_2_out15),
    .sel(and_1_out[3:0]), .en(and_1_out[4]));
  Register #(.width(32)) register_1 (.D(wdata), .en(and_2_out), .clk(clk), .Q(register_1_q), .clr(rst));
  and and_2 (and_2_out, 1'b0, decoder_1_out0);
  Register #(.width(32)) register_2 (.D(wdata), .en(decoder_1_out8), .clk(clk), .Q(register_2_q), .clr(rst));
  Register #(.width(32)) register_3 (.D(wdata), .en(decoder_2_out0), .clk(clk), .Q(register_3_q), .clr(rst));
  Register #(.width(32)) register_4 (.D(wdata), .en(decoder_2_out8), .clk(clk), .Q(register_4_q), .clr(rst));
  Register #(.width(32)) register_5 (.D(wdata), .en(decoder_1_out1), .clk(clk), .Q(register_5_q), .clr(rst));
  Register #(.width(32)) register_6 (.D(wdata), .en(decoder_1_out9), .clk(clk), .Q(register_6_q), .clr(rst));
  Register #(.width(32)) register_7 (.D(wdata), .en(decoder_2_out1), .clk(clk), .Q(register_7_q), .clr(rst));
  Register #(.width(32)) register_8 (.D(wdata), .en(decoder_2_out9), .clk(clk), .Q(register_8_q), .clr(rst));
  Register #(.width(32)) register_9 (.D(wdata), .en(decoder_1_out2), .clk(clk), .Q(register_9_q), .clr(rst));
  Register #(.width(32)) register_10 (.D(wdata), .en(decoder_1_out10), .clk(clk), .Q(register_10_q), .clr(rst));
  Register #(.width(32)) register_11 (.D(wdata), .en(decoder_2_out2), .clk(clk), .Q(register_11_q), .clr(rst));
  Register #(.width(32)) register_12 (.D(wdata), .en(decoder_2_out10), .clk(clk), .Q(register_12_q), .clr(rst));
  Register #(.width(32)) register_13 (.D(wdata), .en(decoder_1_out3), .clk(clk), .Q(register_13_q), .clr(rst));
  Register #(.width(32)) register_14 (.D(wdata), .en(decoder_1_out11), .clk(clk), .Q(register_14_q), .clr(rst));
  Register #(.width(32)) register_15 (.D(wdata), .en(decoder_2_out3), .clk(clk), .Q(register_15_q), .clr(rst));
  Register #(.width(32)) register_16 (.D(wdata), .en(decoder_2_out11), .clk(clk), .Q(register_16_q), .clr(rst));
  Register #(.width(32)) register_17 (.D(wdata), .en(decoder_1_out4), .clk(clk), .Q(register_17_q), .clr(rst));
  Register #(.width(32)) register_18 (.D(wdata), .en(decoder_1_out12), .clk(clk), .Q(register_18_q), .clr(rst));
  Register #(.width(32)) register_19 (.D(wdata), .en(decoder_2_out4), .clk(clk), .Q(register_19_q), .clr(rst));
  Register #(.width(32)) register_20 (.D(wdata), .en(decoder_2_out12), .clk(clk), .Q(register_20_q), .clr(rst));
  Register #(.width(32)) register_21 (.D(wdata), .en(decoder_1_out5), .clk(clk), .Q(register_21_q), .clr(rst));
  Register #(.width(32)) register_22 (.D(wdata), .en(decoder_1_out13), .clk(clk), .Q(register_22_q), .clr(rst));
  Register #(.width(32)) register_23 (.D(wdata), .en(decoder_2_out5), .clk(clk), .Q(register_23_q), .clr(rst));
  Register #(.width(32)) register_24 (.D(wdata), .en(decoder_2_out13), .clk(clk), .Q(register_24_q), .clr(rst));
  Register #(.width(32)) register_25 (.D(wdata), .en(decoder_1_out6), .clk(clk), .Q(register_25_q), .clr(rst));
  Register #(.width(32)) register_26 (.D(wdata), .en(decoder_1_out14), .clk(clk), .Q(register_26_q), .clr(rst));
  Register #(.width(32)) register_27 (.D(wdata), .en(decoder_2_out6), .clk(clk), .Q(register_27_q), .clr(rst));
  Register #(.width(32)) register_28 (.D(wdata), .en(decoder_2_out14), .clk(clk), .Q(register_28_q), .clr(rst));
  Register #(.width(32)) register_29 (.D(wdata), .en(decoder_1_out7), .clk(clk), .Q(register_29_q), .clr(rst));
  Register #(.width(32)) register_30 (.D(wdata), .en(decoder_1_out15), .clk(clk), .Q(register_30_q), .clr(rst));
  Register #(.width(32)) register_31 (.D(wdata), .en(decoder_2_out7), .clk(clk), .Q(register_31_q), .clr(rst));
  Register #(.width(32)) register_32 (.D(wdata), .en(decoder_2_out15), .clk(clk), .Q(register_32_q), .clr(rst));
  Multiplexer #(.select(4), .width(32)) multiplexer_1 (
    .in0(register_1_q), .in1(register_5_q), .in2(register_9_q), .in3(register_13_q), .in4(register_17_q),
    .in5(register_21_q), .in6(register_25_q), .in7(register_29_q), .in8(register_2_q), .in9(register_6_q),
    .in10(register_10_q), .in11(register_14_q), .in12(register_18_q), .in13(register_22_q),
    .in14(register_26_q), .in15(register_30_q), .out(multiplexer_1_out), .sel(raddr1[3:0]));
  Multiplexer #(.select(4), .width(32)) multiplexer_2 (
    .in0(register_1_q), .in1(register_5_q), .in2(register_9_q), .in3(register_13_q), .in4(register_17_q),
    .in5(register_21_q), .in6(register_25_q), .in7(register_29_q), .in8(register_2_q), .in9(register_6_q),
    .in10(register_10_q), .in11(register_14_q), .in12(register_18_q), .in13(register_22_q),
    .in14(register_26_q), .in15(register_30_q), .out(multiplexer_2_out), .sel(raddr2[3:0]));
  Multiplexer #(.select(4), .width(32)) multiplexer_3 (
    .in0(register_3_q), .in1(register_7_q), .in2(register_11_q), .in3(register_15_q), .in4(register_19_q),
    .in5(register_23_q), .in6(register_27_q), .in7(register_31_q), .in8(register_4_q), .in9(register_8_q),
    .in10(register_12_q), .in11(register_16_q), .in12(register_20_q), .in13(register_24_q),
    .in14(register_28_q), .in15(register_32_q), .out(multiplexer_3_out), .sel(raddr1[3:0]));
  Multiplexer #(.select(4), .width(32)) multiplexer_4 (
    .in0(register_3_q), .in1(register_7_q), .in2(register_11_q), .in3(register_15_q), .in4(register_19_q),
    .in5(register_23_q), .in6(register_27_q), .in7(register_31_q), .in8(register_4_q), .in9(register_8_q),
    .in10(register_12_q), .in11(register_16_q), .in12(register_20_q), .in13(register_24_q),
    .in14(register_28_q), .in15(register_32_q), .out(multiplexer_4_out), .sel(raddr2[3:0]));
  not not_2 (not_2_out, raddr1[4]);
  assign bit_extender_2_out = {{31{not_2_out}}, not_2_out};  // Bit_Extender bit_extender_2
  assign bit_extender_3_out = {{31{raddr1[4]}}, raddr1[4]};  // Bit_Extender bit_extender_3
  not not_3 (not_3_out, raddr2[4]);
  assign bit_extender_4_out = {{31{raddr2[4]}}, raddr2[4]};  // Bit_Extender bit_extender_4
  assign and_3_out = bit_extender_3_out & multiplexer_3_out;  // AND_Gate and_3, 32 bits wide
  assign bit_extender_5_out = {{31{not_3_out}}, not_3_out};  // Bit_Extender bit_extender_5
  assign and_4_out = bit_extender_2_out & multiplexer_1_out;  // AND_Gate and_4, 32 bits wide
  assign and_5_out = multiplexer_2_out & bit_extender_5_out;  // AND_Gate and_5, 32 bits wide
  assign and_6_out = bit_extender_4_out & multiplexer_4_out;  // AND_Gate and_6, 32 bits wide
  assign rdata1 = and_4_out | and_3_out;  // OR_Gate or_1, 32 bits wide
  assign rdata2 = and_5_out | and_6_out;  // OR_Gate or_2, 32 bits wide
endmodule

module ram_test (
  input  clk,
  input  [31:0] in_2,
  input  lw,
  input  lbu,
  input  sb,
  input  sw,
  input  [1:0] addr10,
  input  [31:0] rdata2,
  output [31:0] out_9,
  output [31:0] out_10,
  output [31:0] out_11
);

  wire decoder_1_out0, decoder_1_out1, decoder_1_out2, decoder_1_out3, or_1_out, or_2_out, or_3_out,
       or_4_out, or_5_out, or_6_out;
  wire [4:0] bit_extender_1_out, bit_extender_4_out, shifter_1_out, shifter_3_out;
  wire [31:0] and_1_out, and_2_out, bit_extender_2_out, bit_extender_3_out, shifter_2_out, shifter_4_out;

  Decoder #(.select(2)) decoder_1 (
    .out0(decoder_1_out0), .out1(decoder_1_out1), .out2(decoder_1_out2), .out3(decoder_1_out3), .sel(addr10),
    .en(sb));
  assign bit_extender_1_out = {{3{1'b0}}, addr10};  // Bit_Extender bit_extender_1
  or or_1 (or_1_out, lw, lbu);
  or or_2 (or_2_out, sw, decoder_1_out0);
  or or_3 (or_3_out, sw, decoder_1_out1);
  or or_4 (or_4_out, sw, decoder_1_out2);
  or or_5 (or_5_out, sw, decoder_1_out3);
  Shifter #(.width(5)) shifter_1 (.in(bit_extender_1_out), .\dist (3'b011), .out(shifter_1_out));
  or or_6 (or_6_out, sb, sw);
  assign bit_extender_2_out = {{31{sb}}, sb};  // Bit_Extender bit_extender_2
  assign bit_extender_3_out = {{31{sw}}, sw};  // Bit_Extender bit_extender_3
  Shifter #(.width(32)) shifter_2 (.in(rdata2), .\dist (shifter_1_out), .out(shifter_2_out));
  assign and_1_out = shifter_2_out & bit_extender_2_out;  // AND_Gate and_1, 32 bits wide
  assign and_2_out = rdata2 & bit_extender_3_out;  // AND_Gate and_2, 32 bits wide
  RAM #(.addrWidth(24), .asyncread("true"), .byteenables("byteEnables"), .dataWidth(32), .\type ("nonvolatile")) ram_1 (
    .addr(in_2[23:0]), .we(or_6_out), .oe(or_1_out), .clk(clk), .din(out_11), .dout(out_9), .be3(or_5_out),
    .be2(or_4_out), .be1(or_3_out), .be0(or_2_out));
  assign out_11 = and_1_out | and_2_out;  // OR_Gate or_7, 32 bits wide
  assign bit_extender_4_out = {{3{1'b0}}, addr10};  // Bit_Extender bit_extender_4
  Shifter #(.width(5)) shifter_3 (.in(bit_extender_4_out), .\dist (3'b011), .out(shifter_3_out));
  Shifter #(.shift("lr"), .width(32)) shifter_4 (.in(out_9), .\dist (shifter_3_out), .out(shifter_4_out));
  assign out_10 = {{24{1'b0}}, shifter_4_out[7:0]};  // Bit_Extender bit_extender_5

  // Notes on the sheet:
  //   addr<<2
endmodule

module VGA_X_Y (
  input  [31:0] addr,
  output [31:0] X,
  output [31:0] Y
);

  wire [31:0] divider_1_out, subtractor_1_out;

  Subtractor #(.width(32)) subtractor_1 (.a(addr), .b(32'h20000000), .out(subtractor_1_out));  // open: bin, bout
  Divider #(.width(32)) divider_1 (
    .a(subtractor_1_out), .b(32'h4), .out(divider_1_out), .upper({32{1'b0}}));  // open: rem
  Divider #(.width(32)) divider_2 (.a(divider_1_out), .b(32'h100), .out(Y), .upper({32{1'b0}}), .rem(X));
  Subtractor #(.width(32)) subtractor_2 (.a(32'h100));  // open: b, out, bin, bout
  Subtractor #(.width(32)) subtractor_3 (.a(32'h100));  // open: b, out, bin, bout
endmodule
