// Logisim project logisim_sCPU.circ as structural Verilog: 7 circuits, main circuit main
module main (
  input  rst,
  input  in_2,
  input  [31:0] in_3,
  input  lw,
  input  lbu,
  input  clk,
  input  sb,
  input  sw,
  input  [1:0] addr10,
  input  [31:0] rdata2,
  output [31:0] out_11,
  output [31:0] out_12
);

  wire add, addi, and_4_out, and_5_out, decoder_1_out0, decoder_1_out1, decoder_1_out2, decoder_1_out3,
       ebreak, jalr, lbu_t, lui, lw_t, not_2_out, not_3_out, or_2_out, or_5_out, or_6_out, or_7_out,
       or_8_out, or_10_out, or_11_out, or_12_out, or_13_out, or_14_out, or_15_out, sb_t, sw_t, wen;
  wire [4:0] bit_extender_11_out, raddr1, raddr2, shifter_1_out, waddr;
  wire [23:0] pc_1_pc_out;
  wire [31:0] add_rst, and_1_out, and_2_out, and_3_out, and_6_out, and_7_out, and_8_out, and_9_out,
       and_10_out, and_11_out, and_12_out, and_13_out, and_14_out, and_16_out, and_17_out,
       bit_extender_1_out, bit_extender_2_out, bit_extender_3_out, bit_extender_4_out, bit_extender_5_out,
       bit_extender_6_out, bit_extender_7_out, bit_extender_8_out, bit_extender_9_out, bit_extender_10_out,
       bit_extender_12_out, bit_extender_13_out, gpr_1_rdata1, immI, immS, immU, lbu_rst, not_1_out,
       or_1_out, or_3_out, pc_next_dft, ram_1_dout, rdata2_t, shifter_2_out, wdata;
  wire [31:8] lw_rst;
  wire [31:24] pc_1_pc_out_2;

  assign bit_extender_1_out = {{31{jalr}}, jalr};  // Bit_Extender bit_extender_1
  assign and_1_out = add_rst & 32'hffffffe;  // AND_Gate and_1, 32 bits wide
  assign not_1_out = ~bit_extender_1_out;  // NOT_Gate not_1, 32 bits wide
  assign and_2_out = bit_extender_1_out & and_1_out;  // AND_Gate and_2, 32 bits wide
  assign and_3_out = pc_next_dft & not_1_out;  // AND_Gate and_3, 32 bits wide
  assign or_1_out = and_2_out | and_3_out;  // OR_Gate or_1, 32 bits wide
  RAM #(.addrWidth(24), .asyncread("true"), .dataWidth(32), .\type ("nonvolatile")) ram_1 (
    .addr(pc_1_pc_out), .we(1'b0), .oe(1'b1), .clk(clk), .dout(ram_1_dout));  // open: din
  or or_2 (or_2_out, sw_t, sb_t);
  pc pc_1 (.rst(rst), .pc_in(or_1_out), .WE(1'b1), .clk(clk), .pc_out({pc_1_pc_out_2, pc_1_pc_out}));
  GPR gpr_1 (
    .raddr1(raddr1), .clk(clk), .wdata(wdata), .wen(wen), .waddr(waddr), .raddr2(raddr2),
    .rdata1(gpr_1_rdata1), .rdata2(rdata2_t));
  not not_2 (not_2_out, add);
  not not_3 (not_3_out, or_2_out);
  assign bit_extender_2_out = {{31{add}}, add};  // Bit_Extender bit_extender_2
  and and_4 (and_4_out, not_2_out, or_2_out);
  and and_5 (and_5_out, not_3_out, not_2_out);
  Adder #(.width(32)) adder_1 (.a({pc_1_pc_out_2, pc_1_pc_out}), .b(32'h4), .out(pc_next_dft));  // open: cin, cout
  assign and_6_out = rdata2_t & bit_extender_2_out;  // AND_Gate and_6, 32 bits wide
  assign bit_extender_3_out = {{31{and_4_out}}, and_4_out};  // Bit_Extender bit_extender_3
  assign bit_extender_4_out = {{31{and_5_out}}, and_5_out};  // Bit_Extender bit_extender_4
  decode decode_1 (
    .instr(ram_1_dout), .lw(lw_t), .lbu(lbu_t), .rd(waddr), .addi(addi), .rs1(raddr1), .rs2(raddr2),
    .sb(sb_t), .sw(sw_t), .immU(immU), .add(add), .immI(immI), .immS(immS), .lui(lui), .jalr(jalr),
    .ebreak(ebreak));
  assign and_7_out = bit_extender_3_out & immS;  // AND_Gate and_7, 32 bits wide
  assign and_8_out = bit_extender_4_out & immS;  // AND_Gate and_8, 32 bits wide
  assign or_3_out = and_6_out | and_7_out | and_8_out;  // OR_Gate or_3, 32 bits wide
  or or_4 (wen, lw_t, lbu_t, addi, add, lui, jalr);
  Adder #(.width(32)) adder_2 (.a(gpr_1_rdata1), .b(or_3_out), .out(add_rst));  // open: cin, cout
  or or_5 (or_5_out, lw_t, lbu_t);
  or or_6 (or_6_out, sb_t, sw_t);
  or or_7 (or_7_out, lw_t, sw_t);
  or or_8 (or_8_out, lw_t, sw_t, lbu_t, sb_t);
  assign bit_extender_5_out = {{31{lui}}, lui};  // Bit_Extender bit_extender_5
  assign bit_extender_6_out = {{31{add}}, add};  // Bit_Extender bit_extender_6
  assign bit_extender_7_out = {{31{addi}}, addi};  // Bit_Extender bit_extender_7
  assign bit_extender_8_out = {{31{jalr}}, jalr};  // Bit_Extender bit_extender_8
  assign bit_extender_9_out = {{31{lw_t}}, lw_t};  // Bit_Extender bit_extender_9
  assign bit_extender_10_out = {{31{lbu_t}}, lbu_t};  // Bit_Extender bit_extender_10
  assign and_9_out = bit_extender_5_out & immU;  // AND_Gate and_9, 32 bits wide
  assign and_10_out = bit_extender_6_out & add_rst;  // AND_Gate and_10, 32 bits wide
  assign and_11_out = bit_extender_7_out & add_rst;  // AND_Gate and_11, 32 bits wide
  assign and_12_out = bit_extender_8_out & pc_next_dft;  // AND_Gate and_12, 32 bits wide
  assign and_13_out = bit_extender_9_out & {lw_rst, lbu_rst[7:0]};  // AND_Gate and_13, 32 bits wide
  assign and_14_out = bit_extender_10_out & lbu_rst;  // AND_Gate and_14, 32 bits wide
  RAM #(.addrWidth(24), .asyncread("true"), .byteenables("byteEnables"), .dataWidth(32), .\type ("nonvolatile")) ram_2 (
    .addr(add_rst[23:0]), .we(or_6_out), .oe(or_5_out), .clk(clk), .din(rdata2_t),
    .dout({lw_rst, lbu_rst[7:0]}), .be3(or_7_out), .be2(or_7_out), .be1(or_7_out), .be0(or_8_out));
  assign wdata = and_9_out | and_10_out | and_11_out | and_12_out | and_13_out | and_14_out;  // OR_Gate or_9, 32 bits wide
  assign lbu_rst[31:8] = lw_rst & {24{1'b0}};  // AND_Gate and_15, 24 bits wide
  Decoder #(.select(2)) decoder_1 (
    .out0(decoder_1_out0), .out1(decoder_1_out1), .out2(decoder_1_out2), .out3(decoder_1_out3), .sel(addr10),
    .en(sb));
  assign bit_extender_11_out = {{3{1'b0}}, addr10};  // Bit_Extender bit_extender_11
  or or_10 (or_10_out, lw, lbu);
  or or_11 (or_11_out, sw, decoder_1_out0);
  or or_12 (or_12_out, sw, decoder_1_out1);
  or or_13 (or_13_out, sw, decoder_1_out2);
  or or_14 (or_14_out, sw, decoder_1_out3);
  Shifter #(.width(5)) shifter_1 (.in(bit_extender_11_out), .\dist (3'b011), .out(shifter_1_out));
  or or_15 (or_15_out, sb, sw);
  assign bit_extender_12_out = {{31{sb}}, sb};  // Bit_Extender bit_extender_12
  assign bit_extender_13_out = {{31{sw}}, sw};  // Bit_Extender bit_extender_13
  Shifter #(.width(32)) shifter_2 (.in(rdata2), .\dist (shifter_1_out), .out(shifter_2_out));
  assign and_16_out = shifter_2_out & bit_extender_12_out;  // AND_Gate and_16, 32 bits wide
  assign and_17_out = rdata2 & bit_extender_13_out;  // AND_Gate and_17, 32 bits wide
  RAM #(.addrWidth(24), .asyncread("true"), .byteenables("byteEnables"), .dataWidth(32), .\type ("nonvolatile")) ram_3 (
    .addr(in_3[23:0]), .we(or_15_out), .oe(or_10_out), .clk(in_2), .din(out_12), .dout(out_11),
    .be3(or_14_out), .be2(or_13_out), .be1(or_12_out), .be0(or_11_out));
  assign out_12 = and_16_out | and_17_out;  // OR_Gate or_16, 32 bits wide

  // Other names for the same wires on the sheet: lw_rst[7:0] = lbu_rst[7:0]

  // Notes on the sheet:
  //   addr<<2
endmodule

module pc (
  input  rst,
  input  [31:0] pc_in,
  input  WE,
  input  clk,
  output [31:0] pc_out
);

  wire not_1_out;
  wire [31:0] and_1_out, bit_extender_1_out;

  not not_1 (not_1_out, rst);
  assign bit_extender_1_out = {{31{not_1_out}}, not_1_out};  // Bit_Extender bit_extender_1
  assign and_1_out = bit_extender_1_out & pc_in;  // AND_Gate and_1, 32 bits wide
  Register #(.width(32)) pc (.D(and_1_out), .en(WE), .clk(clk), .Q(pc_out));  // open: clr
endmodule

module decode (
  input  [31:0] instr,
  output lw,
  output lbu,
  output [4:0] rd,
  output addi,
  output [4:0] rs1,
  output [4:0] rs2,
  output sb,
  output sw,
  output [31:0] immU,
  output add,
  output [31:0] immI,
  output [31:0] immS,
  output lui,
  output jalr,
  output ebreak
);

  wire decoder_1_out3, decoder_1_out35, decoder_2_out2, decoder_2_out4, decoder_3_out0, decoder_3_out2;

  decode_imm decode_imm_1 (.instr(instr), .immU(immU), .immI(immI), .immS(immS));
  Decoder #(.select(7)) decoder_1 (
    .out3(decoder_1_out3), .out19(addi), .out35(decoder_1_out35), .out51(add), .out55(lui), .out103(jalr),
    .out115(ebreak), .sel(instr[6:0]), .en(1'b1));  // open: out0, out1, out2, out4, out5, out6, out7, out8, out9, out10, out11, out12, out13, out14, out15, out16, out17, out18, out20, out21, out22, out23, out24, out25, out26, out27, out28, out29, out30, out31, out32, out33, out34, out36, out37, out38, out39, out40, out41, out42, out43, out44, out45, out46, out47, out48, out49, out50, out52, out53, out54, out56, out57, out58, out59, out60, out61, out62, out63, out64, out65, out66, out67, out68, out69, out70, out71, out72, out73, out74, out75, out76, out77, out78, out79, out80, out81, out82, out83, out84, out85, out86, out87, out88, out89, out90, out91, out92, out93, out94, out95, out96, out97, out98, out99, out100, out101, out102, out104, out105, out106, out107, out108, out109, out110, out111, out112, out113, out114, out116, out117, out118, out119, out120, out121, out122, out123, out124, out125, out126, out127
  Decoder #(.select(3)) decoder_2 (
    .out2(decoder_2_out2), .out4(decoder_2_out4), .sel(instr[14:12]), .en(1'b1));  // open: out0, out1, out3, out5, out6, out7
  Decoder #(.select(3)) decoder_3 (
    .out0(decoder_3_out0), .out2(decoder_3_out2), .sel(instr[14:12]), .en(1'b1));  // open: out1, out3, out4, out5, out6, out7
  and and_1 (lw, decoder_1_out3, decoder_2_out2);
  and and_2 (lbu, decoder_2_out4, decoder_1_out3);
  and and_3 (sb, decoder_1_out35, decoder_3_out0);
  and and_4 (sw, decoder_3_out2, decoder_1_out35);

  assign rd = instr[11:7];
  assign rs1 = instr[19:15];
  assign rs2 = instr[24:20];

  // Other names for the same wires on the sheet: funct3[2:0] = instr[14:12]
endmodule

module bin_seg (
  input  D,
  input  in_2,
  input  in_3,
  input  A,
  output g,
  output f,
  output e,
  output out_8,
  output c,
  output b,
  output out_11
);

  wire and_1_out, and_2_out, and_3_out, and_4_out, and_5_out, and_6_out, and_7_out, and_8_out, and_9_out,
       and_10_out, and_11_out, and_12_out, and_13_out, and_14_out, and_15_out, and_16_out, and_17_out,
       and_18_out, and_19_out, and_20_out, and_21_out, and_22_out, and_23_out, and_24_out, and_25_out,
       and_26_out, and_27_out, and_28_out, and_29_out, and_30_out, and_31_out, and_32_out, and_33_out,
       and_34_out, and_35_out, not_1_out, not_2_out, not_3_out, not_4_out;

  not not_1 (not_1_out, D);
  not not_2 (not_2_out, in_2);
  not not_3 (not_3_out, in_3);
  not not_4 (not_4_out, A);
  and and_1 (and_1_out, not_2_out, not_4_out);
  and and_2 (and_2_out, not_1_out, in_3);
  and and_3 (and_3_out, not_1_out, in_2, A);
  and and_4 (and_4_out, D, not_2_out, not_3_out);
  and and_5 (and_5_out, D, not_4_out);
  and and_6 (and_6_out, in_2, in_3);
  and and_7 (and_7_out, not_1_out, not_3_out, not_4_out);
  and and_8 (and_8_out, not_1_out, in_3, A);
  and and_9 (and_9_out, not_2_out, not_4_out);
  and and_10 (and_10_out, D, not_3_out, A);
  and and_11 (and_11_out, not_1_out, not_2_out);
  and and_12 (and_12_out, not_1_out, in_2);
  and and_13 (and_13_out, D, not_2_out);
  and and_14 (and_14_out, not_3_out, A);
  and and_15 (and_15_out, not_2_out, not_3_out);
  and and_16 (and_16_out, not_2_out, A);
  and and_17 (and_17_out, in_2, not_3_out, A);
  and and_18 (and_18_out, not_1_out, not_2_out, not_4_out);
  and and_19 (and_19_out, not_2_out, in_3, A);
  and and_20 (and_20_out, D, not_3_out);
  and and_21 (and_21_out, in_2, in_3, not_4_out);
  and and_22 (and_22_out, not_2_out, not_4_out);
  and and_23 (and_23_out, in_3, not_4_out);
  and and_24 (and_24_out, D, in_3);
  and and_25 (and_25_out, D, in_2);
  and and_26 (and_26_out, not_3_out, not_4_out);
  and and_27 (and_27_out, not_1_out, in_2, not_3_out);
  and and_28 (and_28_out, in_2, not_4_out);
  and and_29 (and_29_out, D, not_2_out);
  and and_30 (and_30_out, D, in_3);
  and and_31 (and_31_out, not_2_out, in_3);
  and and_32 (and_32_out, D, not_2_out);
  and and_33 (and_33_out, not_1_out, in_2, not_3_out);
  and and_34 (and_34_out, in_3, not_4_out);
  and and_35 (and_35_out, D, A);
  or or_1 (g, and_1_out, and_2_out, and_3_out, and_4_out, and_5_out, and_6_out);
  or or_2 (f, and_7_out, and_8_out, and_9_out, and_10_out, and_11_out);
  or or_3 (e, and_12_out, and_13_out, and_14_out, and_15_out, and_16_out);
  or or_4 (out_8, and_17_out, and_18_out, and_19_out, and_20_out, and_21_out);
  or or_5 (c, and_22_out, and_23_out, and_24_out, and_25_out);
  or or_6 (b, and_26_out, and_27_out, and_28_out, and_29_out, and_30_out);
  or or_7 (out_11, and_31_out, and_32_out, and_33_out, and_34_out, and_35_out);
endmodule

module decode_imm (
  input  [31:0] instr,
  output [31:0] immU,
  output [31:0] immI,
  output [31:0] immS
);

  assign immI[31:11] = {{20{instr[31]}}, instr[31]};  // Bit_Extender bit_extender_1

  assign immI[10:0] = instr[30:20];
  assign immS = {immI[31:11], instr[30:25], instr[11:7]};
  assign immU = {instr[31:12], {12{1'b0}}};
endmodule

module GPR (
  input  [4:0] raddr1,
  input  clk,
  input  [31:0] wdata,
  input  wen,
  input  [4:0] waddr,
  input  [4:0] raddr2,
  output [31:0] rdata1,
  output [31:0] rdata2
);

  wire and_2_out, decoder_1_out0, decoder_1_out1, decoder_1_out2, decoder_1_out3, decoder_1_out4,
       decoder_1_out5, decoder_1_out6, decoder_1_out7, decoder_1_out8, decoder_1_out9, decoder_1_out10,
       decoder_1_out11, decoder_1_out12, decoder_1_out13, decoder_1_out14, decoder_1_out15, decoder_2_out0,
       decoder_2_out1, decoder_2_out2, decoder_2_out3, decoder_2_out4, decoder_2_out5, decoder_2_out6,
       decoder_2_out7, decoder_2_out8, decoder_2_out9, decoder_2_out10, decoder_2_out11, decoder_2_out12,
       decoder_2_out13, decoder_2_out14, decoder_2_out15, not_1_out, not_2_out, not_3_out;
  wire [4:0] and_1_out, bit_extender_1_out;
  wire [31:0] and_3_out, and_4_out, and_5_out, and_6_out, bit_extender_2_out, bit_extender_3_out,
       bit_extender_4_out, bit_extender_5_out, multiplexer_1_out, multiplexer_2_out, multiplexer_3_out,
       multiplexer_4_out, register_1_q, register_2_q, register_3_q, register_4_q, register_5_q, register_6_q,
       register_7_q, register_8_q, register_9_q, register_10_q, register_11_q, register_12_q, register_13_q,
       register_14_q, register_15_q, register_16_q, register_17_q, register_18_q, register_19_q,
       register_20_q, register_21_q, register_22_q, register_23_q, register_24_q, register_25_q,
       register_26_q, register_27_q, register_28_q, register_29_q, register_30_q, register_31_q,
       register_32_q;

  assign bit_extender_1_out = {{4{wen}}, wen};  // Bit_Extender bit_extender_1
  assign and_1_out = bit_extender_1_out & waddr;  // AND_Gate and_1, 5 bits wide
  not not_1 (not_1_out, and_1_out[4]);
  Decoder #(.select(4)) decoder_1 (
    .out0(decoder_1_out0), .out1(decoder_1_out1), .out2(decoder_1_out2), .out3(decoder_1_out3),
    .out4(decoder_1_out4), .out5(decoder_1_out5), .out6(decoder_1_out6), .out7(decoder_1_out7),
    .out8(decoder_1_out8), .out9(decoder_1_out9), .out10(decoder_1_out10), .out11(decoder_1_out11),
    .out12(decoder_1_out12), .out13(decoder_1_out13), .out14(decoder_1_out14), .out15(decoder_1_out15),
    .sel(and_1_out[3:0]), .en(not_1_out));
  Decoder #(.select(4)) decoder_2 (
    .out0(decoder_2_out0), .out1(decoder_2_out1), .out2(decoder_2_out2), .out3(decoder_2_out3),
    .out4(decoder_2_out4), .out5(decoder_2_out5), .out6(decoder_2_out6), .out7(decoder_2_out7),
    .out8(decoder_2_out8), .out9(decoder_2_out9), .out10(decoder_2_out10), .out11(decoder_2_out11),
    .out12(decoder_2_out12), .out13(decoder_2_out13), .out14(decoder_2_out14), .out15(decoder_2_out15),
    .sel(and_1_out[3:0]), .en(and_1_out[4]));
  Register #(.width(32)) register_1 (.D(wdata), .en(and_2_out), .clk(clk), .Q(register_1_q));  // open: clr
  and and_2 (and_2_out, wen, decoder_1_out0);
  Register #(.width(32)) register_2 (.D(wdata), .en(decoder_1_out8), .clk(clk), .Q(register_2_q));  // open: clr
  Register #(.width(32)) register_3 (.D(wdata), .en(decoder_2_out0), .clk(clk), .Q(register_3_q));  // open: clr
  Register #(.width(32)) register_4 (.D(wdata), .en(decoder_2_out8), .clk(clk), .Q(register_4_q));  // open: clr
  Register #(.width(32)) register_5 (.D(wdata), .en(decoder_1_out1), .clk(clk), .Q(register_5_q));  // open: clr
  Register #(.width(32)) register_6 (.D(wdata), .en(decoder_1_out9), .clk(clk), .Q(register_6_q));  // open: clr
  Register #(.width(32)) register_7 (.D(wdata), .en(decoder_2_out1), .clk(clk), .Q(register_7_q));  // open: clr
  Register #(.width(32)) register_8 (.D(wdata), .en(decoder_2_out9), .clk(clk), .Q(register_8_q));  // open: clr
  Register #(.width(32)) register_9 (.D(wdata), .en(decoder_1_out2), .clk(clk), .Q(register_9_q));  // open: clr
  Register #(.width(32)) register_10 (.D(wdata), .en(decoder_1_out10), .clk(clk), .Q(register_10_q));  // open: clr
  Register #(.width(32)) register_11 (.D(wdata), .en(decoder_2_out2), .clk(clk), .Q(register_11_q));  // open: clr
  Register #(.width(32)) register_12 (.D(wdata), .en(decoder_2_out10), .clk(clk), .Q(register_12_q));  // open: clr
  Register #(.width(32)) register_13 (.D(wdata), .en(decoder_1_out3), .clk(clk), .Q(register_13_q));  // open: clr
  Register #(.width(32)) register_14 (.D(wdata), .en(decoder_1_out11), .clk(clk), .Q(register_14_q));  // open: clr
  Register #(.width(32)) register_15 (.D(wdata), .en(decoder_2_out3), .clk(clk), .Q(register_15_q));  // open: clr
  Register #(.width(32)) register_16 (.D(wdata), .en(decoder_2_out11), .clk(clk), .Q(register_16_q));  // open: clr
  Register #(.width(32)) register_17 (.D(wdata), .en(decoder_1_out4), .clk(clk), .Q(register_17_q));  // open: clr
  Register #(.width(32)) register_18 (.D(wdata), .en(decoder_1_out12), .clk(clk), .Q(register_18_q));  // open: clr
  Register #(.width(32)) register_19 (.D(wdata), .en(decoder_2_out4), .clk(clk), .Q(register_19_q));  // open: clr
  Register #(.width(32)) register_20 (.D(wdata), .en(decoder_2_out12), .clk(clk), .Q(register_20_q));  // open: clr
  Register #(.width(32)) register_21 (.D(wdata), .en(decoder_1_out5), .clk(clk), .Q(register_21_q));  // open: clr
  Register #(.width(32)) register_22 (.D(wdata), .en(decoder_1_out13), .clk(clk), .Q(register_22_q));  // open: clr
  Register #(.width(32)) register_23 (.D(wdata), .en(decoder_2_out5), .clk(clk), .Q(register_23_q));  // open: clr
  Register #(.width(32)) register_24 (.D(wdata), .en(decoder_2_out13), .clk(clk), .Q(register_24_q));  // open: clr
  Register #(.width(32)) register_25 (.D(wdata), .en(decoder_1_out6), .clk(clk), .Q(register_25_q));  // open: clr
  Register #(.width(32)) register_26 (.D(wdata), .en(decoder_1_out14), .clk(clk), .Q(register_26_q));  // open: clr
  Register #(.width(32)) register_27 (.D(wdata), .en(decoder_2_out6), .clk(clk), .Q(register_27_q));  // open: clr
  Register #(.width(32)) register_28 (.D(wdata), .en(decoder_2_out14), .clk(clk), .Q(register_28_q));  // open: clr
  Register #(.width(32)) register_29 (.D(wdata), .en(decoder_1_out7), .clk(clk), .Q(register_29_q));  // open: clr
  Register #(.width(32)) register_30 (.D(wdata), .en(decoder_1_out15), .clk(clk), .Q(register_30_q));  // open: clr
  Register #(.width(32)) register_31 (.D(wdata), .en(decoder_2_out7), .clk(clk), .Q(register_31_q));  // open: clr
  Register #(.width(32)) register_32 (.D(wdata), .en(decoder_2_out15), .clk(clk), .Q(register_32_q));  // open: clr
  Multiplexer #(.select(4), .width(32)) multiplexer_1 (
    .in0(register_1_q), .in1(register_5_q), .in2(register_9_q), .in3(register_13_q), .in4(register_17_q),
    .in5(register_21_q), .in6(register_25_q), .in7(register_29_q), .in8(register_2_q), .in9(register_6_q),
    .in10(register_10_q), .in11(register_14_q), .in12(register_18_q), .in13(register_22_q),
    .in14(register_26_q), .in15(register_30_q), .out(multiplexer_1_out), .sel(raddr1[3:0]));
  Multiplexer #(.select(4), .width(32)) multiplexer_2 (
    .in0(register_1_q), .in1(register_5_q), .in2(register_9_q), .in3(register_13_q), .in4(register_17_q),
    .in5(register_21_q), .in6(register_25_q), .in7(register_29_q), .in8(register_2_q), .in9(register_6_q),
    .in10(register_10_q), .in11(register_14_q), .in12(register_18_q), .in13(register_22_q),
    .in14(register_26_q), .in15(register_30_q), .out(multiplexer_2_out), .sel(raddr2[3:0]));
  Multiplexer #(.select(4), .width(32)) multiplexer_3 (
    .in0(register_3_q), .in1(register_7_q), .in2(register_11_q), .in3(register_15_q), .in4(register_19_q),
    .in5(register_23_q), .in6(register_27_q), .in7(register_31_q), .in8(register_4_q), .in9(register_8_q),
    .in10(register_12_q), .in11(register_16_q), .in12(register_20_q), .in13(register_24_q),
    .in14(register_28_q), .in15(register_32_q), .out(multiplexer_3_out), .sel(raddr1[3:0]));
  Multiplexer #(.select(4), .width(32)) multiplexer_4 (
    .in0(register_3_q), .in1(register_7_q), .in2(register_11_q), .in3(register_15_q), .in4(register_19_q),
    .in5(register_23_q), .in6(register_27_q), .in7(register_31_q), .in8(register_4_q), .in9(register_8_q),
    .in10(register_12_q), .in11(register_16_q), .in12(register_20_q), .in13(register_24_q),
    .in14(register_28_q), .in15(register_32_q), .out(multiplexer_4_out), .sel(raddr2[3:0]));
  not not_2 (not_2_out, raddr1[4]);
  assign bit_extender_2_out = {{31{not_2_out}}, not_2_out};  // Bit_Extender bit_extender_2
  assign bit_extender_3_out = {{31{raddr1[4]}}, raddr1[4]};  // Bit_Extender bit_extender_3
  not not_3 (not_3_out, raddr2[4]);
  assign bit_extender_4_out = {{31{raddr2[4]}}, raddr2[4]};  // Bit_Extender bit_extender_4
  assign and_3_out = bit_extender_3_out & multiplexer_3_out;  // AND_Gate and_3, 32 bits wide
  assign bit_extender_5_out = {{31{not_3_out}}, not_3_out};  // Bit_Extender bit_extender_5
  assign and_4_out = bit_extender_2_out & multiplexer_1_out;  // AND_Gate and_4, 32 bits wide
  assign and_5_out = multiplexer_2_out & bit_extender_5_out;  // AND_Gate and_5, 32 bits wide
  assign and_6_out = bit_extender_4_out & multiplexer_4_out;  // AND_Gate and_6, 32 bits wide
  assign rdata1 = and_4_out | and_3_out;  // OR_Gate or_1, 32 bits wide
  assign rdata2 = and_5_out | and_6_out;  // OR_Gate or_2, 32 bits wide
endmodule

module ram_test (
  input  clk,
  input  [31:0] in_2,
  input  lw,
  input  lbu,
  input  sb,
  input  sw,
  input  [1:0] addr10,
  input  [31:0] rdata2,
  output [31:0] out_9,
  output [31:0] out_10
);

  wire decoder_1_out0, decoder_1_out1, decoder_1_out2, decoder_1_out3, or_1_out, or_2_out, or_3_out,
       or_4_out, or_5_out, or_6_out;
  wire [4:0] bit_extender_1_out, shifter_1_out;
  wire [31:0] and_1_out, and_2_out, bit_extender_2_out, bit_extender_3_out, shifter_2_out;

  Decoder #(.select(2)) decoder_1 (
    .out0(decoder_1_out0), .out1(decoder_1_out1), .out2(decoder_1_out2), .out3(decoder_1_out3), .sel(addr10),
    .en(sb));
  assign bit_extender_1_out = {{3{1'b0}}, addr10};  // Bit_Extender bit_extender_1
  or or_1 (or_1_out, lw, lbu);
  or or_2 (or_2_out, sw, decoder_1_out0);
  or or_3 (or_3_out, sw, decoder_1_out1);
  or or_4 (or_4_out, sw, decoder_1_out2);
  or or_5 (or_5_out, sw, decoder_1_out3);
  Shifter #(.width(5)) shifter_1 (.in(bit_extender_1_out), .\dist (3'b011), .out(shifter_1_out));
  or or_6 (or_6_out, sb, sw);
  assign bit_extender_2_out = {{31{sb}}, sb};  // Bit_Extender bit_extender_2
  assign bit_extender_3_out = {{31{sw}}, sw};  // Bit_Extender bit_extender_3
  Shifter #(.width(32)) shifter_2 (.in(rdata2), .\dist (shifter_1_out), .out(shifter_2_out));
  assign and_1_out = shifter_2_out & bit_extender_2_out;  // AND_Gate and_1, 32 bits wide
  assign and_2_out = rdata2 & bit_extender_3_out;  // AND_Gate and_2, 32 bits wide
  RAM #(.addrWidth(24), .asyncread("true"), .byteenables("byteEnables"), .dataWidth(32), .\type ("nonvolatile")) ram_1 (
    .addr(in_2[23:0]), .we(or_6_out), .oe(or_1_out), .clk(clk), .din(out_10), .dout(out_9), .be3(or_5_out),
    .be2(or_4_out), .be1(or_3_out), .be0(or_2_out));
  assign out_10 = and_1_out | and_2_out;  // OR_Gate or_7, 32 bits wide

  // Notes on the sheet:
  //   addr<<2
endmodule
